# Fritzing sketch khach (saved by Fritzing 0.9.6b)
breadboards: 1

parts:
  DHT1 = Humidity and Temperature Sensor DHT11
  KF-1 = KF-301 Relay [package=THT]
  U1 = ESP32-38PinWide [part_number=ESP32-38PinWide]

nets:
  N1: DHT1.Vcc, U1.3.3
  N2: DHT1.Data-signal, U1.GPIO26
  N3: DHT1.GND_2, U1.GND
  N4: KF-1.signal, U1.GPIO25
  N5: KF-1.power, U1.VIN
  N6: KF-1.ground, U1.GPIO11

custom parts:
  Humidity and Temperature Sensor DHT11: Digital relative humidity & temperature sensor DHT11
  KF-301 Relay: KF-301
  ESP32-38PinWide: Generic 38-Pin ESP32 with wide format (only access to one side of pins on a breadboard) based on Stephen Lilley's HiLetgo ESP-WROOM-32 ESP32 ESP-32S Development Board.
