# Fritzing sketch vuon (saved by Fritzing 0.9.6b)
breadboards: 1

parts:
  부품1 = FC-28 Soil Hygrometer Module - Probe
  부품2 = FC-28 Soil Hygrometer Module
  U1 = ESP32-38PinWide [part_number=ESP32-38PinWide]
  KF-1 = KF-301 Relay [package=THT]

nets:
  N1: 부품1.POS, 부품2.POS
  N2: 부품1.NEG, 부품2.NEG
  N3: 부품2.VCC, U1.3.3
  N4: 부품2.GND, U1.GPIO11, KF-1.ground
  N5: 부품2.AO, U1.GPIO39
  N6: U1.GPIO25, KF-1.signal
  N7: U1.VIN, KF-1.power

custom parts:
  FC-28 Soil Hygrometer Module - Probe: The FC-28 is a soil hygrometer module that uses the Texas Instruments LM393 comparator chip to provide an analog measurement of soil humidity.
  FC-28 Soil Hygrometer Module: The FC-28 is a soil hygrometer module that uses the Texas Instruments LM393 comparator chip to provide an analog measurement of soil humidity. The digital output is high when soil moisture is over a certain threshold, as determined by adjusting the potentiometer.
  ESP32-38PinWide: Generic 38-Pin ESP32 with wide format (only access to one side of pins on a breadboard) based on Stephen Lilley's HiLetgo ESP-WROOM-32 ESP32 ESP-32S Development Board.
  KF-301 Relay: KF-301
